# Fritzing sketch WaterDropachine (saved by Fritzing 0.9.4)
breadboards: 1

parts:
  U1 = TRANSCHIPTC5747 [package=camera_sfv24r-2st_2]
  IC1 = ULN2803A [package=THT]
  U2 = Optocoupler [package=THT]
  U3 = Optocoupler [package=THT]
  R1 = Resistor [tolerance=±5% resistance=330 package="0402 [SMD]"]
  L2 = Solenoid
  U4 = TRANSCHIPTC5747 [package=camera_sfv24r-2st_2]
  Part1 = Arduino Uno (Rev3) - ICSP
  R2 = Resistor [tolerance=±5% resistance=330 package="0402 [SMD]"]
  VCC1 = 4 x AAA Battery Mount
  LED1 = smd LED [color="Blue (470nm)" package="1206 [SMD]"]
  LED2 = smd LED [color="Green (555nm)" package="1206 [SMD]"]
  R3 = Resistor [tolerance=±5% resistance=330 package="0402 [SMD]"]
  LED3 = smd LED [color="Red (633nm)" package="1206 [SMD]"]

nets:
  N1: U1.DGND, U2.Pin_5
  N2: U1.DOUT_0, U2.Pin_4
  N3: IC1.0V, U2.Pin_2, U3.Pin_2, Part1.GND, LED1.cathode, LED2.cathode, LED3.cathode
  N4: IC1.COM_-_Common, L2.pin2, VCC1.+
  N5: U3.Pin_4, U4.DOUT_0
  N6: U3.Pin_5, U4.DGND
  N7: R1.Pin_0, Part1.D4, LED2.anode
  N8: Part1.D8, R3.Pin_1
  N9: Part1.D3_PWM, R2.Pin_0, LED3.anode
  N10: LED1.anode, R3.Pin_0

// code stored in the sketch: WaterDropachine.ino

/* Water Drop Machine V1
*
* Sketch that control the waterDropMachin created to perform water drop photography.
* The system is based on arduino and a solenoid valve that drops water at a regular time interval.
* The flash and the camero trigger are automatically triggered at predefined interval.
* By Antranik Zekian, 2021 - part of the code freely inspired from the code "Water Drop Controller V4" by Gareth Bellamy
*
*/


//Constant declaration
const int DELAY_CAM_FLASH = 100; // delay between the camera triggering and the flash triggering
const int CAMERA_BUTTON_HOLD_TIME = 100; // delay between the camera triggering and the flash triggering

//Arduino pin declaration
const int camPIN = 3;        //Set camPIN (camera) to pin 3
const int flashPIN = 4;        //Set camPIN (camera) to pin 3
const int solPIN = 8;        //Set solPIN (soleniod valve) to pin 8

int inputs[5] = {0, 0, 0, 0, 0}; //{1st drop size, 2nd drop size, valve delay, camera delay, iterations}




void displayValues()
{

  int i =0;
      
  while (i<5)
  {
    Serial.println("Display value in memory:");
    Serial.print(inputs[i]);
    Serial.print("|");  
    i++;
  }
  
  Serial.print("|");  

}

/*
Function that launch the water dropping and capture actions
DropOneSize - 1st drop size input variable (milliseconds)
DropTwoSize - 2nd drop size input variable (milliseconds)
SolDelay - Set delay between drops (milliseconds)
CamDelay - Set delay between drops and camera activation (milliseconds)
*/

void launchCapture(int DropOneSize,int DropTwoSize,int SolDelay,int CamDelay)
{
  
  digitalWrite (solPIN, HIGH);            //Opens solenoid valve
  delay (DropOneSize);                    //Valve stays open for time value DropOneSize -> define 1st drop size
  digitalWrite (solPIN, LOW);             //Closes solenoid valve
  
  delay (SolDelay);                       //Time delay between drops
  digitalWrite (solPIN, HIGH);            //Opens solenoid valve
  delay (DropTwoSize);                    //Valve stays open for time value DropTwoSize - 2nd drop size
  digitalWrite (solPIN, LOW);             //Closes solenoid valve
  
  delay (CamDelay);                       //Time delay for camera activation
  
  digitalWrite (camPIN, HIGH);            //Sets camPIN to high - fires camera
  delay (DELAY_CAM_FLASH);                //Holds camPIN high for 100 milliseconds before firing the flash
  digitalWrite (flashPIN, HIGH);          //Sets flashcamPIN to high - trigger flash
  delay (CAMERA_BUTTON_HOLD_TIME);        //Holds camPIN high for 100 milliseconds to ensure signal
  digitalWrite (flashPIN, LOW);             //Sets flashPIN to low
  digitalWrite (camPIN, LOW);               //Sets camPIN to low
  
}



void setup() {

  //Initial Configuration of Arduino setup
  
   Serial.begin(9600);                //Start the Serial Monitor
   pinMode (camPIN, OUTPUT);          //Set camPIN to an output
   pinMode (flashPIN, OUTPUT);        //Set flashPIN  to an output
   pinMode (solPIN, OUTPUT);          //Set solPIN to an output

}


void loop() {
   
//Here is where the time delays will be entered into the serial monitor

   Serial.println("Enter the settings - Format: ");
   Serial.println("1st drop size (ms) | 2nd drop size (ms) in milliseconds | Valve Delay (ms) | Camera Delay (ms) | Iteration");               //Print text asking for 1st drop size
   
   if (Serial.available() > 0) {

    char buff[32];
    int returned = Serial.readBytesUntil('\n', buff, 32);
    buff[31] = 0;    
    char *values = strtok(buff, "|");
    
    // Check data typed and convert them into int
    if (returned == 0) {
    
      Serial.println("ERROR: invalid data received");
    
    } else {
    
      Serial.println("INFO: valid data received");
      
      int i = 0;
      
      while (values != NULL) {
        
        int val = atoi(values);
        Serial.println(val);
        inputs[i] = val;
        i++;
        values = strtok(NULL, "|");
      
      }
      
      // check if a valid number of inputs was found
      if (i == 5) {
        
        displayValues();

        int Iteration = inputs[4];
        int j=0;
        
        while (j < Iteration )
        {
          Serial.print("INFO: iteration #");
          Serial.print(j);
          launchCapture(inputs[0],inputs[1],inputs[2],inputs[3]);
          j++;
          Serial.println("   COMPLETED");
        }
        
      }else{
        
        Serial.println("ERROR: number of values received incorrect");
        
      }
      
    }

   }
   
   Serial.println("INFO: end of loop()");
}
